// Logisim project SynthBite16.circ as structural Verilog: 1 circuit, main circuit SynthBite16
module SynthBite16 (
  input  in_1,
  input  [15:0] in_2,
  input  [15:0] in_3,
  input  in_4
);

  wire AC_p1, AC_p2, AC_p18, AC_p19, AC_p20, AC_p21, AC_p22, AC_p23, AC_p24, AC_p25, AC_p26, AC_p27, AC_p28,
       AC_p29, adder_1_cout, and_2_out, and_3_out, controlled_buffer_1_out, controlled_buffer_2_out,
       controlled_buffer_3_out, controlled_buffer_4_out, controlled_buffer_5_out, controlled_buffer_6_out,
       controlled_buffer_7_out, controlled_buffer_8_out, controlled_buffer_9_out, controlled_buffer_10_out,
       controlled_buffer_11_out, controlled_buffer_12_out, controlled_buffer_13_out,
       controlled_buffer_14_out, controlled_buffer_15_out, controlled_buffer_16_out,
       controlled_buffer_47_out, controlled_buffer_48_out, controlled_buffer_49_out,
       controlled_buffer_50_out, controlled_buffer_51_out, controlled_buffer_52_out,
       controlled_buffer_53_out, controlled_buffer_54_out, controlled_buffer_55_out,
       controlled_buffer_56_out, controlled_buffer_57_out, controlled_buffer_58_out,
       controlled_buffer_59_out, controlled_buffer_60_out, controlled_buffer_61_out, decoder_1_out0,
       decoder_1_out1, decoder_1_out2, decoder_1_out3, decoder_2_out0, decoder_2_out1, decoder_2_out3,
       decoder_2_out10, decoder_2_out11, decoder_2_out13, MasterClock_out, nand_1_out, not_2_out, or_2_out,
       or_3_out, shift_register_1_p1, subtractor_1_bout, undriven, undriven_2, undriven_5, undriven_6,
       undriven_7, undriven_8, undriven_9, undriven_10;
  wire [0:0] DR_q;
  wire [3:0] CWR_q;
  wire [9:0] CAR_q, undriven_4;
  wire [11:0] controlled_buffer_17_out, PC_q;
  wire [15:0] adder_1_out, adder_2_out, and_1_out, DR_q_2, IR_q, multiplexer_1_out, not_1_out, or_1_out,
       rand_q, register_2_q, shift_register_1_p4, subtractor_1_out, undriven_3, xor_1_out;
  wire [15:15] controlled_buffer_29_out;
  wire [23:0] CNTRL_MEM_data, CWR_q_2;

  Controlled_Buffer controlled_buffer_1 (.out(controlled_buffer_1_out), .en(undriven));  // open: in
  Controlled_Buffer controlled_buffer_2 (.out(controlled_buffer_2_out), .en(undriven));  // open: in
  Controlled_Buffer controlled_buffer_3 (.out(controlled_buffer_3_out), .en(undriven));  // open: in
  Controlled_Buffer controlled_buffer_4 (.out(controlled_buffer_4_out), .en(undriven));  // open: in
  Controlled_Buffer controlled_buffer_5 (.out(controlled_buffer_5_out), .en(undriven));  // open: in
  Controlled_Buffer controlled_buffer_6 (.out(controlled_buffer_6_out), .en(undriven));  // open: in
  Controlled_Buffer controlled_buffer_7 (.out(controlled_buffer_7_out), .en(undriven));  // open: in
  Controlled_Buffer controlled_buffer_8 (.out(controlled_buffer_8_out), .en(undriven));  // open: in
  Controlled_Buffer controlled_buffer_9 (.out(controlled_buffer_9_out), .en(undriven));  // open: in
  Controlled_Buffer controlled_buffer_10 (.out(controlled_buffer_10_out), .en(undriven));  // open: in
  Controlled_Buffer controlled_buffer_11 (.out(controlled_buffer_11_out), .en(undriven));  // open: in
  Controlled_Buffer controlled_buffer_12 (.out(controlled_buffer_12_out), .en(undriven));  // open: in
  Controlled_Buffer controlled_buffer_13 (.out(controlled_buffer_13_out), .en(undriven));  // open: in
  Controlled_Buffer controlled_buffer_14 (.out(controlled_buffer_14_out), .en(undriven));  // open: in
  Controlled_Buffer controlled_buffer_15 (.out(controlled_buffer_15_out), .en(undriven));  // open: in
  Controlled_Buffer controlled_buffer_16 (.out(controlled_buffer_16_out), .en(undriven));  // open: in
  Clock MasterClock (.out(MasterClock_out));
  LED led_1 (.in(MasterClock_out));
  Register #(.width(16)) DR (
    .D({{4{controlled_buffer_29_out[15]}}, controlled_buffer_17_out}), .en(decoder_2_out10),
    .clk(MasterClock_out), .Q({DR_q_2[14:0], DR_q[0]}), .clr(undriven_2));
  LedBar #(.matrixcols(4)) ledbar_1 (
    .led0(controlled_buffer_29_out[15]), .led1(controlled_buffer_29_out[15]),
    .led2(controlled_buffer_29_out[15]), .led3(controlled_buffer_29_out[15]));
  DotMatrix #(.matrixcols(16), .matrixrows(1)) dotmatrix_1 (
    .col0(controlled_buffer_29_out[15]), .col1(controlled_buffer_29_out[15]),
    .col2(controlled_buffer_29_out[15]), .col3(controlled_buffer_29_out[15]),
    .col4(controlled_buffer_17_out[11]), .col5(controlled_buffer_17_out[10]),
    .col6(controlled_buffer_17_out[9]), .col7(controlled_buffer_17_out[8]),
    .col8(controlled_buffer_17_out[7]), .col9(controlled_buffer_17_out[6]),
    .col10(controlled_buffer_17_out[5]), .col11(controlled_buffer_17_out[4]),
    .col12(controlled_buffer_17_out[3]), .col13(controlled_buffer_17_out[2]),
    .col14(controlled_buffer_17_out[1]), .col15(controlled_buffer_17_out[0]));
  assign controlled_buffer_17_out[0] = decoder_1_out3 ? PC_q[0] : 1'bz;  // Controlled_Buffer controlled_buffer_17
  assign controlled_buffer_17_out[1] = decoder_1_out3 ? PC_q[1] : 1'bz;  // Controlled_Buffer controlled_buffer_18
  assign controlled_buffer_17_out[2] = decoder_1_out3 ? PC_q[2] : 1'bz;  // Controlled_Buffer controlled_buffer_19
  assign controlled_buffer_17_out[3] = decoder_1_out3 ? PC_q[3] : 1'bz;  // Controlled_Buffer controlled_buffer_20
  assign controlled_buffer_17_out[4] = decoder_1_out3 ? PC_q[4] : 1'bz;  // Controlled_Buffer controlled_buffer_21
  assign controlled_buffer_17_out[5] = decoder_1_out3 ? PC_q[5] : 1'bz;  // Controlled_Buffer controlled_buffer_22
  assign controlled_buffer_17_out[6] = decoder_1_out3 ? PC_q[6] : 1'bz;  // Controlled_Buffer controlled_buffer_23
  assign controlled_buffer_17_out[7] = decoder_1_out3 ? PC_q[7] : 1'bz;  // Controlled_Buffer controlled_buffer_24
  assign controlled_buffer_17_out[8] = decoder_1_out3 ? PC_q[8] : 1'bz;  // Controlled_Buffer controlled_buffer_25
  assign controlled_buffer_17_out[9] = decoder_1_out3 ? PC_q[9] : 1'bz;  // Controlled_Buffer controlled_buffer_26
  assign controlled_buffer_17_out[10] = decoder_1_out3 ? PC_q[10] : 1'bz;  // Controlled_Buffer controlled_buffer_27
  assign controlled_buffer_17_out[11] = decoder_1_out3 ? PC_q[11] : 1'bz;  // Controlled_Buffer controlled_buffer_28
  assign controlled_buffer_29_out[15] = decoder_1_out3 ? in_4 : 1'bz;  // Controlled_Buffer controlled_buffer_29
  Register #(.width(12)) PC (
    .D(controlled_buffer_17_out), .en(decoder_2_out3), .clk(MasterClock_out), .Q(PC_q));  // open: clr
  Register #(.width(16)) IR (
    .D({{4{controlled_buffer_29_out[15]}}, controlled_buffer_17_out}), .en(decoder_2_out11),
    .clk(MasterClock_out), .Q(IR_q));  // open: clr
  Register register_1 (.en(in_1), .clk(MasterClock_out));  // open: D, Q, clr
  Adder #(.width(16)) adder_1 (
    .a({DR_q_2[14:0], DR_q[0]}), .b({{4{controlled_buffer_29_out[15]}}, controlled_buffer_17_out}),
    .out(adder_1_out), .cin(DR_q_2[15]), .cout(adder_1_cout));
  Subtractor #(.width(16)) subtractor_1 (
    .a({DR_q_2[14:0], DR_q[0]}), .b({{4{controlled_buffer_29_out[15]}}, controlled_buffer_17_out}),
    .out(subtractor_1_out), .bin(DR_q_2[15]), .bout(subtractor_1_bout));
  assign or_1_out = {{4{controlled_buffer_29_out[15]}}, controlled_buffer_17_out} | {DR_q_2[14:0], DR_q[0]};  // OR_Gate or_1, 16 bits wide
  Counter #(.max('h3f), .width(6)) tim (.clk(MasterClock_out));  // open: clr, load, up, count, D, carry, Q
  or or_2 (or_2_out, adder_1_cout, subtractor_1_bout);
  assign xor_1_out = {{4{controlled_buffer_29_out[15]}}, controlled_buffer_17_out} ^ {DR_q_2[14:0], DR_q[0]};  // XOR_Gate xor_1, 16 bits wide
  or or_3 (or_3_out, or_2_out, DR_q[0]);
  // Shift_Register #(.length(1), .width(16)) shift_register_1: pin names not known; wires that end beside it: shift_register_1_p1, MasterClock_out, {{4{controlled_buffer_29_out[15]}}, controlled_buffer_17_out}, shift_register_1_p4
  assign and_1_out = {{4{controlled_buffer_29_out[15]}}, controlled_buffer_17_out} & {DR_q_2[14:0], DR_q[0]};  // AND_Gate and_1, 16 bits wide
  Adder #(.width(16)) adder_2 (
    .a(in_3), .b({{4{controlled_buffer_29_out[15]}}, controlled_buffer_17_out}), .out(adder_2_out));  // open: cin, cout
  Register #(.width(16)) \rand  (.D(undriven_3), .clk(MasterClock_out), .Q(rand_q));  // open: en, clr
  Hex_Digit_Display hex_digit_display_1 (.value(shift_register_1_p4[15:12]));  // open: dp
  Hex_Digit_Display hex_digit_display_2 (.value(shift_register_1_p4[11:8]));  // open: dp
  Hex_Digit_Display hex_digit_display_3 (.value(shift_register_1_p4[7:4]));  // open: dp
  Hex_Digit_Display hex_digit_display_4 (.value(shift_register_1_p4[3:0]));  // open: dp
  Register #(.width(10)) CAR (.D(undriven_4), .en(1'b1), .clk(MasterClock_out), .Q(CAR_q));  // open: clr
  assign not_1_out = ~{DR_q_2[14:0], DR_q[0]};  // NOT_Gate not_1, 16 bits wide
  ROM #(.addrWidth(10), .dataWidth(24)) CNTRL_MEM (.addr(CAR_q), .data(CNTRL_MEM_data));
  Register #(.trigger("falling"), .width(24)) CWR (
    .D(CNTRL_MEM_data), .en(1'b1), .clk(MasterClock_out), .Q({CWR_q_2[23:12], CWR_q, CWR_q_2[7:0]}));  // open: clr
  Multiplexer #(.select(4), .width(16)) multiplexer_1 (
    .in0({DR_q_2[14:0], DR_q[0]}), .in1(not_1_out), .in2(adder_1_out), .in3(subtractor_1_out),
    .in4(or_1_out), .in5(xor_1_out), .in6(and_1_out), .in7(DR_q_2), .in8(DR_q_2), .in9(rand_q),
    .in10(adder_2_out), .in14(in_2), .in15(in_2), .out(multiplexer_1_out), .sel(CWR_q));  // open: in11, in12, in13
  DotMatrix #(.matrixcols(24), .matrixrows(1)) dotmatrix_2 (
    .col0(CWR_q_2[0]), .col1(CWR_q_2[1]), .col2(CWR_q_2[2]), .col3(CWR_q_2[3]), .col4(CWR_q_2[4]),
    .col5(CWR_q_2[5]), .col6(CWR_q_2[6]), .col7(CWR_q_2[7]), .col8(CWR_q[0]), .col9(CWR_q[1]),
    .col10(CWR_q[2]), .col11(CWR_q[3]), .col12(CWR_q_2[12]), .col13(CWR_q_2[13]), .col14(CWR_q_2[14]),
    .col15(CWR_q_2[15]), .col16(CWR_q_2[16]), .col17(CWR_q_2[17]), .col18(CWR_q_2[18]), .col19(CWR_q_2[19]),
    .col20(CWR_q_2[20]), .col21(CWR_q_2[21]), .col22(CWR_q_2[22]), .col23(CWR_q_2[23]));
  nand nand_1 (nand_1_out, CWR_q[1], CWR_q[0]);
  not not_2 (not_2_out, CWR_q[2]);
  and and_2 (and_2_out, not_2_out, nand_1_out);
  and and_3 (and_3_out, CWR_q[3], and_2_out);
  // Shift_Register #(.length(16)) AC: pin names not known; wires that end beside it: AC_p1, AC_p2, and_3_out, MasterClock_out, DR_q_2[15], multiplexer_1_out[0], multiplexer_1_out[1], multiplexer_1_out[2], multiplexer_1_out[3], multiplexer_1_out[4], multiplexer_1_out[5], multiplexer_1_out[6], multiplexer_1_out[7], multiplexer_1_out[8], multiplexer_1_out[9], multiplexer_1_out[10], multiplexer_1_out[11], AC_p18, AC_p19, AC_p20, AC_p21, AC_p22, AC_p23, AC_p24, AC_p25, AC_p26, AC_p27, AC_p28, AC_p29
  RAM #(.addrWidth(12), .asyncread("true"), .dataWidth(16), .databus("bidir")) MEM (
    .addr(PC_q), .we(decoder_2_out1), .oe(decoder_1_out1), .clk(MasterClock_out),
    .data({{4{controlled_buffer_29_out[15]}}, controlled_buffer_17_out}));
  Decoder #(.enable("false"), .select(4)) decoder_1 (
    .out0(decoder_1_out0), .out1(decoder_1_out1), .out2(decoder_1_out2), .out3(decoder_1_out3),
    .sel(CWR_q_2[3:0]));  // open: out4, out5, out6, out7, out8, out9, out10, out11, out12, out13, out14, out15
  Decoder #(.enable("false"), .select(4)) decoder_2 (
    .out0(decoder_2_out0), .out1(decoder_2_out1), .out2(AC_p2), .out3(decoder_2_out3),
    .out10(decoder_2_out10), .out11(decoder_2_out11), .out12(shift_register_1_p1), .out13(decoder_2_out13),
    .sel(CWR_q_2[7:4]));  // open: out4, out5, out6, out7, out8, out9, out14, out15
  D_Flip_Flop carry (.D(or_3_out), .clk(MasterClock_out));  // open: Q, Qn, preset, reset
  assign controlled_buffer_17_out[0] = decoder_1_out2 ? AC_p18 : 1'bz;  // Controlled_Buffer controlled_buffer_30
  assign controlled_buffer_17_out[1] = decoder_1_out2 ? AC_p19 : 1'bz;  // Controlled_Buffer controlled_buffer_31
  assign controlled_buffer_17_out[2] = decoder_1_out2 ? AC_p20 : 1'bz;  // Controlled_Buffer controlled_buffer_32
  assign controlled_buffer_17_out[3] = decoder_1_out2 ? AC_p21 : 1'bz;  // Controlled_Buffer controlled_buffer_33
  assign controlled_buffer_17_out[4] = decoder_1_out2 ? AC_p22 : 1'bz;  // Controlled_Buffer controlled_buffer_34
  assign controlled_buffer_17_out[5] = decoder_1_out2 ? AC_p23 : 1'bz;  // Controlled_Buffer controlled_buffer_35
  assign controlled_buffer_17_out[6] = decoder_1_out2 ? AC_p24 : 1'bz;  // Controlled_Buffer controlled_buffer_36
  assign controlled_buffer_17_out[7] = decoder_1_out2 ? AC_p25 : 1'bz;  // Controlled_Buffer controlled_buffer_37
  assign controlled_buffer_17_out[8] = decoder_1_out2 ? AC_p26 : 1'bz;  // Controlled_Buffer controlled_buffer_38
  assign controlled_buffer_17_out[9] = decoder_1_out2 ? AC_p27 : 1'bz;  // Controlled_Buffer controlled_buffer_39
  assign controlled_buffer_17_out[10] = decoder_1_out2 ? AC_p28 : 1'bz;  // Controlled_Buffer controlled_buffer_40
  assign controlled_buffer_17_out[11] = decoder_1_out2 ? AC_p29 : 1'bz;  // Controlled_Buffer controlled_buffer_41
  assign controlled_buffer_29_out[15] = decoder_1_out2 ? undriven_5 : 1'bz;  // Controlled_Buffer controlled_buffer_42
  assign controlled_buffer_29_out[15] = decoder_1_out2 ? undriven_6 : 1'bz;  // Controlled_Buffer controlled_buffer_43
  assign controlled_buffer_29_out[15] = decoder_1_out2 ? undriven_7 : 1'bz;  // Controlled_Buffer controlled_buffer_44
  assign controlled_buffer_29_out[15] = decoder_1_out2 ? undriven_8 : 1'bz;  // Controlled_Buffer controlled_buffer_45
  LED led_2 (.in(decoder_1_out0));
  LED led_3 (.in(decoder_2_out0));
  D_Flip_Flop d_ff_1 (.D(decoder_2_out13), .clk(MasterClock_out), .Q(DR_q_2[15]));  // open: Qn, preset, reset
  Counter #(.max('h7), .width(3)) SR ();  // open: clr, load, up, count, clk, D, carry, Q
  Register #(.width(16)) register_2 (.Q(register_2_q));  // open: D, en, clk, clr
  Register #(.width(16)) register_3 ();  // open: D, en, clk, Q, clr
  Register #(.width(16)) register_4 ();  // open: D, en, clk, Q, clr
  Register #(.width(16)) register_5 (.clr(undriven_10));  // open: D, en, clk, Q
  Controlled_Buffer controlled_buffer_46 (.en(undriven_9));  // open: in, out
  Controlled_Buffer controlled_buffer_47 (.out(controlled_buffer_47_out), .en(undriven_9));  // open: in
  Controlled_Buffer controlled_buffer_48 (.out(controlled_buffer_48_out), .en(undriven_9));  // open: in
  Controlled_Buffer controlled_buffer_49 (.out(controlled_buffer_49_out), .en(undriven_9));  // open: in
  Controlled_Buffer controlled_buffer_50 (.out(controlled_buffer_50_out), .en(undriven_9));  // open: in
  Controlled_Buffer controlled_buffer_51 (.out(controlled_buffer_51_out), .en(undriven_9));  // open: in
  Controlled_Buffer controlled_buffer_52 (.out(controlled_buffer_52_out), .en(undriven_9));  // open: in
  Controlled_Buffer controlled_buffer_53 (.out(controlled_buffer_53_out), .en(undriven_9));  // open: in
  Controlled_Buffer controlled_buffer_54 (.out(controlled_buffer_54_out), .en(undriven_9));  // open: in
  Controlled_Buffer controlled_buffer_55 (.out(controlled_buffer_55_out), .en(undriven_9));  // open: in
  Controlled_Buffer controlled_buffer_56 (.out(controlled_buffer_56_out), .en(undriven_9));  // open: in
  Controlled_Buffer controlled_buffer_57 (.out(controlled_buffer_57_out), .en(undriven_9));  // open: in
  Controlled_Buffer controlled_buffer_58 (.out(controlled_buffer_58_out), .en(undriven_9));  // open: in
  Controlled_Buffer controlled_buffer_59 (.out(controlled_buffer_59_out), .en(undriven_9));  // open: in
  Controlled_Buffer controlled_buffer_60 (.out(controlled_buffer_60_out), .en(undriven_9));  // open: in
  Controlled_Buffer controlled_buffer_61 (.out(controlled_buffer_61_out), .en(undriven_9));  // open: in
  Register #(.width(16)) register_6 ();  // open: D, en, clk, Q, clr
  Register #(.width(16)) register_7 ();  // open: D, en, clk, Q, clr
  Register #(.width(16)) register_8 ();  // open: D, en, clk, Q, clr
  Register #(.width(16)) register_9 ();  // open: D, en, clk, Q, clr

  // Notes on the sheet:
  //   CLOCK
  //   SYSTEM BUS
  //   16 LINES
  //   PRESENT BUS VALUES
  //   ALU
  //   LEAST SIGNIFICANT LINE
  //   MOST SIGNIFICANT LINE
  //   OUTPUT
  //   this line is just a place holder
  //   CONTROL UNIT
  //   PRESENT CONTROL
  //   AC RESET ASYNC
  //   ACC SHIFT(L)
  //   NONE
  //   MEM OUT ENABLE
  //   ACC ON BUS
  //   PC ON BUS
  //   NONE
  //   AC PARLLEL LOAD
  //   PC LOAD
  //   DR LOAD
  //   IR LOAD
  //   OUT LOAD
  //   SRL IN
  //   PUT ON BUS
  //   MEM WRITE ENABLE
  //   SERIAL IN
  //   LOAD FROM BUS
endmodule
